# Fritzing sketch Miss Angry Bot (saved by Fritzing 0.9.0b)
breadboards: 1

parts:
  part = Arduino Uno (Rev3)
  LED1 = RGB LED (com. cathode, rgb) [package="5 mm [THT]"]
  R1 = Resistor [package="2010 [SMD]"]
  R2 = Resistor [package="2010 [SMD]"]
  R3 = Resistor [package="2010 [SMD]"]
  R4 = Rotary Potentiometer (Small) [maximum_resistance=100kΩ package=THT]
  J1 = Piezo Speaker

nets:
  N1: part.A1, R4.wiper
  N2: part.D9_PWM, R3.Pin_1
  N3: part.D10_PWM/SS, R1.Pin_1
  N4: part.D11_PWM/MOSI, R2.Pin_1
  N5: part.D7, J1.pin2
  N6: part.5V, R4.leg2
  N7: part.GND, LED1.common_cathode, R4.leg1, J1.pin1
  N8: LED1.red_anode, R3.Pin_0
  N9: LED1.green_anode, R2.Pin_0
  N10: LED1.blue_anode, R1.Pin_0
